// Logisim project Question 4.circ as structural Verilog: 1 circuit, main circuit main
module main (
  input  i0,
  input  i1,
  input  i2,
  output A,
  output B,
  output C,
  output D,
  output E,
  output F,
  output G,
  output H
);

  and _000 (A, ~i0, ~i1, ~i2);  // AND_Gate
  and _001 (B, ~i0, ~i1, i2);  // AND_Gate
  and _010 (C, ~i0, i1, ~i2);  // AND_Gate
  and _011 (D, ~i0, i1, i2);  // AND_Gate
  and _100 (E, i0, ~i1, ~i2);  // AND_Gate
  and _101 (F, i0, ~i1, i2);  // AND_Gate
  and _110 (G, i0, i1, ~i2);  // AND_Gate
  and _111 (H, i0, i1, i2);
endmodule
