// Logisim project Question 5.circ as structural Verilog: 1 circuit, main circuit main
module main (
  input  A,
  input  B,
  input  C,
  output X,
  output M,
  output O,
  output N,
  output Y
);

  wire and_1_out, not_1_out, not_4_out, not_5_out, or_2_out;

  not not_1 (not_1_out, B);
  and and_1 (and_1_out, B, C);
  or or_1 (M, A, not_1_out);
  not not_2 (N, and_1_out);
  not not_3 (O, or_2_out);
  or or_2 (or_2_out, M, N);
  not not_4 (not_4_out, M);
  not not_5 (not_5_out, O);
  and and_2 (X, not_4_out, O);
  or or_3 (Y, not_5_out, N);
endmodule
