// Logisim project Question 6.circ as structural Verilog: 1 circuit, main circuit main
module main (
  input  A,
  input  B,
  input  C,
  output X,
  output Y
);

  wire _000_out, _001_out, _010_out, _011_out, _101_out;

  and _000 (_000_out, ~A, ~B, ~C);  // AND_Gate
  and _001 (_001_out, ~A, ~B, C);  // AND_Gate
  and _010 (_010_out, ~A, B, ~C);  // AND_Gate
  and _011 (_011_out, ~A, B, C);  // AND_Gate
  // AND_Gate _100 has open pins: in0=A, in2=B, in4=C, out=open
  and _101 (_101_out, A, ~B, C);  // AND_Gate
  // AND_Gate _110 has open pins: in0=A, in2=B, in4=C, out=open
  // AND_Gate _111 has open pins: in0=A, in2=B, in4=C, out=open
  or or_1 (X, _000_out, _001_out, _010_out, _011_out);
  or or_2 (Y, _011_out, _101_out);
endmodule
