// Logisim project final question.circ as structural Verilog: 1 circuit, main circuit main
module main (
  input  A,
  input  B,
  input  C,
  output Y
);

  wire transistor_1_out, transistor_3_out, transistor_5_out, transistor_8_out, transistor_9_out,
       transistor_10_out, transistor_13_out, transistor_14_out, transistor_20_out;

  Transistor transistor_1 (.in(1'b1), .out(transistor_1_out), .gate(A));
  Transistor #(.\type ("n")) transistor_2 (.in(1'b0), .out(transistor_1_out), .gate(A));
  Transistor transistor_3 (.in(1'b1), .out(transistor_3_out), .gate(B));
  Transistor #(.\type ("n")) transistor_4 (.in(1'b0), .out(transistor_3_out), .gate(B));
  Transistor transistor_5 (.in(1'b1), .out(transistor_5_out), .gate(B));
  Transistor transistor_6 (.in(1'b1), .out(transistor_5_out), .gate(C));
  Transistor #(.\type ("n")) transistor_7 (.in(transistor_8_out), .out(transistor_5_out), .gate(transistor_1_out));
  Transistor #(.\type ("n")) transistor_8 (.in(transistor_9_out), .out(transistor_8_out), .gate(B));
  Transistor #(.\type ("n")) transistor_9 (.in(1'b0), .out(transistor_9_out), .gate(C));
  Transistor transistor_10 (.in(1'b1), .out(transistor_10_out), .gate(transistor_3_out));
  Transistor transistor_11 (.in(1'b1), .out(transistor_10_out), .gate(A));
  Transistor #(.\type ("n")) transistor_12 (.in(transistor_13_out), .out(transistor_10_out), .gate(transistor_3_out));
  Transistor #(.\type ("n")) transistor_13 (.in(transistor_14_out), .out(transistor_13_out), .gate(A));
  Transistor #(.\type ("n")) transistor_14 (.in(1'b0), .out(transistor_14_out), .gate(C));
  Transistor transistor_15 (.in(1'b1), .out(transistor_5_out), .gate(transistor_1_out));
  Transistor transistor_16 (.in(1'b1), .out(transistor_10_out), .gate(C));
  Transistor transistor_17 (.in(1'b1), .out(Y), .gate(transistor_5_out));
  Transistor transistor_18 (.in(1'b1), .out(Y), .gate(transistor_10_out));
  Transistor #(.\type ("n")) transistor_19 (.in(transistor_20_out), .out(Y), .gate(transistor_5_out));
  Transistor #(.\type ("n")) transistor_20 (.in(1'b0), .out(transistor_20_out), .gate(transistor_10_out));
endmodule
