// Logisim project reversed final question.circ as structural Verilog: 1 circuit, main circuit main
module main (
  input  A,
  input  B,
  input  C,
  output Y
);

  wire transistor_1_out, transistor_3_out, transistor_4_out, transistor_5_out, transistor_7_out,
       transistor_11_out, transistor_12_out, transistor_17_out;

  Transistor transistor_1 (.in(1'b1), .out(transistor_1_out), .gate(A));
  Transistor #(.\type ("n")) transistor_2 (.in(1'b0), .out(transistor_1_out), .gate(A));
  Transistor #(.\type ("n")) transistor_3 (.in(1'b0), .out(transistor_3_out), .gate(transistor_1_out));
  Transistor transistor_4 (.in(1'b1), .out(transistor_4_out), .gate(transistor_1_out));
  Transistor transistor_5 (.in(1'b1), .out(transistor_5_out), .gate(B));
  Transistor #(.\type ("n")) transistor_6 (.in(1'b0), .out(transistor_5_out), .gate(B));
  Transistor transistor_7 (.in(transistor_4_out), .out(transistor_7_out), .gate(B));
  Transistor transistor_8 (.in(transistor_7_out), .out(transistor_3_out), .gate(C));
  Transistor #(.\type ("n")) transistor_9 (.in(1'b0), .out(transistor_3_out), .gate(B));
  Transistor #(.\type ("n")) transistor_10 (.in(1'b0), .out(transistor_3_out), .gate(C));
  Transistor #(.\type ("n")) transistor_11 (.in(1'b0), .out(transistor_11_out), .gate(A));
  Transistor transistor_12 (.in(1'b1), .out(transistor_12_out), .gate(A));
  Transistor transistor_13 (.in(transistor_12_out), .gate(transistor_5_out));  // open: out
  Transistor transistor_14 (.out(transistor_11_out), .gate(C));  // open: in
  Transistor #(.\type ("n")) transistor_15 (.in(1'b0), .out(transistor_11_out), .gate(transistor_5_out));
  Transistor #(.\type ("n")) transistor_16 (.in(1'b0), .out(transistor_11_out), .gate(C));
  Transistor transistor_17 (.in(1'b1), .out(transistor_17_out), .gate(transistor_11_out));
  Transistor transistor_18 (.in(transistor_17_out), .out(Y), .gate(transistor_3_out));
  Transistor #(.\type ("n")) transistor_19 (.in(1'b0), .out(Y), .gate(transistor_11_out));
  Transistor #(.\type ("n")) transistor_20 (.in(1'b0), .out(Y), .gate(transistor_3_out));
endmodule
