// Logisim project decrementer.circ as structural Verilog: 3 circuits, main circuit main
module main (
  input  A11,
  input  A10,
  input  A9,
  input  A8,
  input  A7,
  input  A6,
  input  A5,
  input  A4,
  input  A3,
  input  A2,
  input  A1,
  input  A0,
  output X11,
  output X10,
  output X9,
  output X8,
  output X7,
  output X6,
  output X5,
  output X4,
  output X3,
  output X2,
  output X1,
  output X0
);

  wire decr1bit_1_carryout, decr1bit_2_carryout, decr1bit_3_carryout, decr1bit_4_carryout,
       decr1bit_5_carryout, decr1bit_6_carryout, decr1bit_7_carryout, decr1bit_8_carryout,
       decr1bit_9_carryout, decr1bit_10_carryout, decrbit0_1_carryout;

  DecrBit0 decrbit0_1 (.A(A0), .Sum(X0), .Carryout(decrbit0_1_carryout));
  Decr1Bit decr1bit_1 (.Cin(decrbit0_1_carryout), .A(A1), .Sum(X1), .Carryout(decr1bit_1_carryout));
  Decr1Bit decr1bit_2 (.Cin(decr1bit_1_carryout), .A(A2), .Sum(X2), .Carryout(decr1bit_2_carryout));
  Decr1Bit decr1bit_3 (.Cin(decr1bit_2_carryout), .A(A3), .Sum(X3), .Carryout(decr1bit_3_carryout));
  Decr1Bit decr1bit_4 (.Cin(decr1bit_3_carryout), .A(A4), .Sum(X4), .Carryout(decr1bit_4_carryout));
  Decr1Bit decr1bit_5 (.Cin(decr1bit_4_carryout), .A(A5), .Sum(X5), .Carryout(decr1bit_5_carryout));
  Decr1Bit decr1bit_6 (.Cin(decr1bit_5_carryout), .A(A6), .Sum(X6), .Carryout(decr1bit_6_carryout));
  Decr1Bit decr1bit_7 (.Cin(decr1bit_6_carryout), .A(A7), .Sum(X7), .Carryout(decr1bit_7_carryout));
  Decr1Bit decr1bit_8 (.Cin(decr1bit_7_carryout), .A(A8), .Sum(X8), .Carryout(decr1bit_8_carryout));
  Decr1Bit decr1bit_9 (.Cin(decr1bit_8_carryout), .A(A9), .Sum(X9), .Carryout(decr1bit_9_carryout));
  Decr1Bit decr1bit_10 (.Cin(decr1bit_9_carryout), .A(A10), .Sum(X10), .Carryout(decr1bit_10_carryout));
  Decr1Bit decr1bit_11 (.Cin(decr1bit_10_carryout), .A(A11), .Sum(X11));  // open: Carryout

  // Notes on the sheet:
  //   Do not introduce any other input or output pins in the main circuit.
  //   INPUT SECTION: Do not change anything here!
  //   You may only change the values of the inputs for testing using the hand tool.
  //   The output of the splitter (12 bits wide) should be the input to your logic.
  //   To your logic
  //   OUTPUT SECTION: Do not change anything here!
  //   Do not introduce any other input or output pins in the main circuit.
  //   The input to the splitter (12 bits wide) should come from the output of your logic.
endmodule

module Decr1Bit (
  input  Cin,
  input  A,
  output Sum,
  output Carryout
);

  wire and_1_out;

  and and_1 (and_1_out, ~Cin, A);  // AND_Gate
  and and_2 (Carryout, Cin, ~A);  // AND_Gate
  or or_1 (Sum, and_1_out, Carryout);
endmodule

module DecrBit0 (
  input  A,
  output Sum,
  output Carryout
);

  not not_1 (Carryout, A);

  assign Sum = Carryout;
endmodule
