// Logisim project h4p2.circ as structural Verilog: 1 circuit, main circuit main
module main (
  input  S1,
  input  S0,
  input  In,
  output S1n,
  output S0n,
  output Out
);

  wire _000_out, _001_out, _010_out, _011_out, _100_out, _101_out, _110_out;

  and _000 (_000_out, ~S1, ~S0, ~In);  // AND_Gate
  and _001 (_001_out, ~S1, ~S0, In);  // AND_Gate
  and _010 (_010_out, ~S1, S0, ~In);  // AND_Gate
  and _011 (_011_out, ~S1, S0, In);  // AND_Gate
  and _100 (_100_out, S1, ~S0, ~In);  // AND_Gate
  and _101 (_101_out, S1, ~S0, In);  // AND_Gate
  and _110 (_110_out, S1, S0, ~In);  // AND_Gate
  // AND_Gate _111 has open pins: in0=S1, in1=S0, in2=In, out=open
  or u_s1n (S1n, _001_out, _011_out, _100_out, _110_out);
  or u_s0n (S0n, _000_out, _010_out, _011_out, _100_out, _101_out, _110_out);
  or u_Out (Out, _000_out, _011_out);

  // Notes on the sheet:
  //   INPUT SECTION: Do not change anything here!
  //   You may only change the values of the inputs for testing using the hand tool.
  //   Do not introduce any other input or output pins in the main circuit.
  //   S1 and S0 represent the current state. In is the input to the state machine.
  //   To your logic
  //   OUTPUT SECTION: Do not change anything here!
  //   Do not introduce any other input or output pins in the main circuit.
  //   S1n and S0n represent the next state. Out is the output of the state machine.
  //   From your logic
endmodule
