// Logisim project h4p3.circ as structural Verilog: 1 circuit, main circuit main
module main (
  input  In,
  output S2,
  output S1,
  output S0,
  output Out
);

  wire _0000_out, _0010_out, _0100_out, _0101_out, _0110_out, _0111_out, _1000_out, _1001_out, _1010_out,
       _1011_out, _1100_out, clock_1_out, S0n_out, S1n_out, S2n_out;

  and _0000 (_0000_out, ~S2, ~S1, ~S0, ~In);  // AND_Gate
  // AND_Gate _0001 has open pins: in0=S2, in1=S1, in2=S0, in3=In, out=open
  and _0010 (_0010_out, ~S2, ~S1, S0, ~In);  // AND_Gate
  // AND_Gate _0011 has open pins: in0=S2, in1=S1, in2=S0, in3=In, out=open
  and _1100 (_1100_out, S2, S1, ~S0, ~In);  // AND_Gate
  // AND_Gate _1101 has open pins: in0=S2, in1=S1, in2=S0, in3=In, out=open
  and _1000 (_1000_out, S2, ~S1, ~S0, ~In);  // AND_Gate
  and _1001 (_1001_out, S2, ~S1, ~S0, In);  // AND_Gate
  and _0110 (_0110_out, ~S2, S1, S0, ~In);  // AND_Gate
  and _0111 (_0111_out, ~S2, S1, S0, In);  // AND_Gate
  and _1010 (_1010_out, S2, ~S1, S0, ~In);  // AND_Gate
  and _1011 (_1011_out, S2, ~S1, S0, In);  // AND_Gate
  and _0100 (_0100_out, ~S2, S1, ~S0, ~In);  // AND_Gate
  and _0101 (_0101_out, ~S2, S1, ~S0, In);  // AND_Gate
  or S2n (S2n_out, _0010_out, _1100_out, _1001_out, _0111_out);
  or S1n (S1n_out, _0010_out, _1000_out, _0110_out, _1011_out);
  or S0n (S0n_out, _0000_out, _1000_out, _0110_out, _0111_out, _1010_out, _0100_out);
  Clock clock_1 (.out(clock_1_out));
  or u_Out (Out, _0100_out, _0101_out);
  D_Flip_Flop d_ff_1 (.clk(clock_1_out), .D(S2n_out), .Q(S2));  // open: Qn, preset, en, reset
  D_Flip_Flop d_ff_2 (.clk(clock_1_out), .D(S1n_out), .Q(S1));  // open: Qn, preset, en, reset
  D_Flip_Flop d_ff_3 (.clk(clock_1_out), .D(S0n_out), .Q(S0));  // open: Qn, preset, en, reset

  // Notes on the sheet:
  //   In is the input to the state machine.
  //   INPUT SECTION: Do not change anything here!
  //   You may only change the values of the inputs for testing using the hand tool.
  //   Do not introduce any other input or output pins in the main circuit.
  //   To your circuit
  //   OUTPUT SECTION: Do not change anything here!
  //   Do not introduce any other input or output pins in the main circuit.
  //   S2, S1, and S0 represent the state. Out is the output of the state machine.
  //   From your circuit
endmodule
