// Logisim project Decoder.circ as structural Verilog: 1 circuit, main circuit main
module main (
  input  A,
  input  B,
  output W,
  output X,
  output Y,
  output Z
);

  and _00 (W, ~A, ~B);  // AND_Gate
  and _01 (X, ~A, B);  // AND_Gate
  and _10 (Y, A, ~B);  // AND_Gate
  and _11 (Z, A, B);
endmodule
