// Logisim project NAND.circ as structural Verilog: 1 circuit, main circuit main
module main (
  input  A,
  input  B,
  output out_3
);

  wire transistor_3_out;

  Transistor transistor_1 (.in(1'b1), .out(out_3), .gate(A));
  Transistor #(.\type ("n")) transistor_2 (.in(transistor_3_out), .out(out_3), .gate(B));
  Transistor #(.\type ("n")) transistor_3 (.in(1'b0), .out(transistor_3_out), .gate(A));
  Transistor transistor_4 (.in(1'b1), .out(out_3), .gate(B));
endmodule
