// Logisim project table to gates.circ as structural Verilog: 1 circuit, main circuit main
module main (
  input  A,
  input  B,
  input  C,
  output X
);

  wire _000_out, _001_out, _010_out, _011_out, _100_out, _101_out, _110_out, _111_out, Xor_out;

  and _000 (_000_out, ~A, ~B, ~C);  // AND_Gate
  and _001 (_001_out, ~A, ~B, C);  // AND_Gate
  and _010 (_010_out, ~A, B, ~C);  // AND_Gate
  and _100 (_100_out, A, ~B, ~C);  // AND_Gate
  and _011 (_011_out, ~A, B, C);  // AND_Gate
  and _101 (_101_out, A, ~B, C);  // AND_Gate
  and _110 (_110_out, A, B, ~C);  // AND_Gate
  and _111 (_111_out, A, B, C);
  xor Xor (Xor_out, _011_out, _101_out);
  not not_1 (X, Xor_out);
endmodule
