// Logisim project incrementer.circ as structural Verilog: 3 circuits, main circuit main
module main (
  input  [7:0] in_1,
  output [7:0] out_2
);

  wire sub2_1_carryout, sub_1_carryout, sub_2_carryout, sub_3_carryout, sub_4_carryout, sub_5_carryout,
       sub_6_carryout;

  sub2 sub2_1 (.A(in_1[0]), .sum(out_2[0]), .Carryout(sub2_1_carryout));
  sub sub_1 (.A(in_1[1]), .Cin(sub2_1_carryout), .Sum(out_2[1]), .Carryout(sub_1_carryout));
  sub sub_2 (.A(in_1[2]), .Cin(sub_1_carryout), .Sum(out_2[2]), .Carryout(sub_2_carryout));
  sub sub_3 (.A(in_1[3]), .Cin(sub_2_carryout), .Sum(out_2[3]), .Carryout(sub_3_carryout));
  sub sub_4 (.A(in_1[4]), .Cin(sub_3_carryout), .Sum(out_2[4]), .Carryout(sub_4_carryout));
  sub sub_5 (.A(in_1[5]), .Cin(sub_4_carryout), .Sum(out_2[5]), .Carryout(sub_5_carryout));
  sub sub_6 (.A(in_1[6]), .Cin(sub_5_carryout), .Sum(out_2[6]), .Carryout(sub_6_carryout));
  sub sub_7 (.A(in_1[7]), .Cin(sub_6_carryout), .Sum(out_2[7]));  // open: Carryout
endmodule

module sub (
  input  A,
  input  Cin,
  output Sum,
  output Carryout
);

  wire _01_out, _10_out;

  and _01 (_01_out, ~A, Cin);  // AND_Gate
  and _10 (_10_out, A, ~Cin);  // AND_Gate
  and _11 (Carryout, A, Cin);
  or or_1 (Sum, _01_out, _10_out);
endmodule

module sub2 (
  input  A,
  output sum,
  output Carryout
);

  not not_1 (sum, A);

  assign Carryout = A;
endmodule
