// Logisim project State Machine.circ as structural Verilog: 1 circuit, main circuit main
module main (
  input  \input ,
  output \output 
);

  wire _01_out, Clock_out, Current_state;

  Clock Clock (.out(Clock_out));
  D_Flip_Flop d_ff_1 (.clk(Clock_out), .D(\input ), .Q(Current_state));  // open: Qn, preset, en, reset
  and _01 (_01_out, ~\input , Current_state);  // AND_Gate
  D_Flip_Flop d_ff_2 (.clk(Clock_out), .D(_01_out), .Q(\output ));  // open: Qn, preset, en, reset

  // Other names for the same wires on the sheet: Next_state = \input 
endmodule
